# Fritzing sketch BuildIndicator_breadboard_schematic (saved by Fritzing 0.9.3b)
breadboards: 1

parts:
  U3 = NodeMCU V1.0
  NEOPIXEL1 = Neopixel Strip -- White (60/m)
  Squix1 = OLED 0.96" 128x64 I2C SSD1306
  NEOPIXEL2 = Neopixel Strip -- White (60/m)

nets:
  N1: U3.D2, NEOPIXEL1.+5V#1
  N2: U3.D3, Squix1.SCA
  N3: U3.D4, Squix1.SCL
  3V3: U3.3V3, Squix1.VCC
  GND: U3.GND, NEOPIXEL1.GND, Squix1.GND, NEOPIXEL2.GND
  N4: U3.RSV#40, NEOPIXEL1.DI, NEOPIXEL2.DI
  N5: NEOPIXEL1.+5V#6, NEOPIXEL2.+5V

notes:
  8x WS2812B

custom parts:
  NodeMCU V1.0: ESP8266 based NodeMCU
  Neopixel Strip -- White (60/m): Neopixel Strip, White, 60 pixels per meter.
